# Fritzing sketch Base_Arduino_board (saved by Fritzing 0.7.11b)
breadboards: 1

parts:
  ATMega328 = atmega328 [package=dip]
  XTAL1 = Crystal [frequency="16 Mhz" package=THT]
  C1 = Ceramic Capacitor [capacitance=22pF package="100 mil [THT, multilayer]"]
  C2 = Ceramic Capacitor [capacitance=22pF package="100 mil [THT, multilayer]"]
  RST = Pushbutton [package="[THT]"]
  Digital = female pin header, 5 pins [form="♀ (female)"]
  Digital_2 = female pin header, 4 pins [form="♀ (female)"]
  Digital_3 = female pin header, 5 pins [form="♀ (female)"]
  Analog_IN = female pin header, 6 pins [form="♀ (female)"]
  Alim_5v = Screw terminal - 2 pins [package=THT]
  RST_2 = female pin header, 1 pin [form="♀ (female)"]

nets:
  N1: ATMega328.RESET, RST.Pin_1, RST.Pin_2, RST_2.pin1
  N2: ATMega328.D0_(RX), Digital_3.pin1
  N3: ATMega328.D1_(TX), Digital_3.pin2
  N4: ATMega328.D2, Digital_3.pin3
  N5: ATMega328.D3_(PWM), Digital_3.pin4
  N6: ATMega328.D4, Digital_3.pin5
  N7: ATMega328.VCC, ATMega328.AVCC, ATMega328.AREF, RST.Pin_3, RST.Pin_4, Alim_5v.pin2
  N8: ATMega328.GND, C1.1, C2.0, Alim_5v.pin1
  N9: ATMega328.XLAT1, XTAL1.pin_0, C2.1
  N10: ATMega328.XLAT2, XTAL1.pin_1, C1.0
  N11: ATMega328.D5_(PWM), Digital_2.pin1
  N12: ATMega328.D6_(PWM), Digital_2.pin2
  N13: ATMega328.D7, Digital_2.pin3
  N14: ATMega328.D8, Digital_2.pin4
  N15: ATMega328.D9_(PWM), Digital.pin5
  N16: ATMega328.D10_(PWM), Digital.pin4
  N17: ATMega328.D11_(PWM), Digital.pin3
  N18: ATMega328.D12, Digital.pin2
  N19: ATMega328.D13, Digital.pin1
  N20: ATMega328.A0, Analog_IN.pin6
  N21: ATMega328.A1, Analog_IN.pin5
  N22: ATMega328.A2, Analog_IN.pin4
  N23: ATMega328.A3, Analog_IN.pin3
  N24: ATMega328.A4, Analog_IN.pin2
  N25: ATMega328.A5, Analog_IN.pin1

notes:
  Main board
  Basic ATMega328 - P.O - r2
